# Fritzing sketch RingDimmer (saved by Fritzing 0.9.3b)

parts:
  Part1 = Adafruit Pro Trinket 3.3V 12MHz [part_number="Adafruit #2010"]
  Part2 = Adafruit Pro Trinket LiIon/LiPoly Backpack [part_number="Adafruit #2124"]
  Part3 = Lithium Ion Battery Pack 3.7V 6600mAh [part_number=353]  # not connected
  Part4 = 24 NeoPixel Ring [part_number=1586]
  U1 = POT [package=pot_alpha_rv16af-20]
  S1 = Toggle Switch [package=THT]

nets:
  GND: Part1.GND, Part2.GND, Part4.GND, U1.E
  N1: Part1.VBAT, Part2.VBAT, Part4.VDD
  N2: Part1.VBUS, Part2.VBUS
  N3: Part1.+3V3, U1.A
  N4: Part1.A0, U1.S
  N5: Part2.SW2, S1.COM
  N6: Part2.SW1, S1.L1

custom parts:
  Adafruit Pro Trinket 3.3V 12MHz: rinket's got a big sister in town - the Pro Trinket 3V! Pro Trinket combines everything you love about Trinket with the familiarity of the core Arduino chip, the ATmega328. It's like an Arduino Pro Mini with more pins and USB tossed in. Trinket's a year old now, and while its been great to see tons of tiny projects, sometimes you just need more pins, more FLASH, and more RAM. That's why we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
  Adafruit Pro Trinket LiIon/LiPoly Backpack: If you have a Pro Trinket you probably know it's the perfect little size for a portable project. This LiPoly backpack makes it really easy to do! Instead of wiring 2 or 3 boards together to make a charging system, this little PCB sits on top of the Pro Trinket and allows a LiPoly/LiIon battery to plug in. When the Pro Trinket USB port is powered, the battery is recharged automatically. Unplug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
  Lithium Ion Battery Pack 3.7V 6600mAh: This lithium ion pack is made of 3 balanced 2200mAh cells for a total of 6600mA capacity! The cells are connected in parallel and spot-welded to a protection circuit that provides over-voltage, under-voltage and over-current protection. Each cell can provide 0.5C of current (1.1 A per) so all together the peak current you can draw is over 3.3 Amps. Note that these batteries are not designed to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
  24 NeoPixel Ring: 24 ultra bright smart LED NeoPixels are arranged in a circle with 2.6" (66mm) outer diameter. The rings are 'chainable' - connect the output pin of one to the input pin of another. Use only one microcontroller pin to control as many as you can chain together! Each LED is addressable as the driver chip is inside the LED. Each one has ~18mA constant current drive so the color will be very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
